# Fritzing sketch Discobot_hardware (saved by Fritzing 0.8.7b)
breadboards: 1

parts:
  Raspberry_Pi_1 = Raspberry Pi 3
  U1 = WS2812 RGB LED strip
  J2 = Basic Servo
  J1 = Basic Servo
  MD09B2 = A4988 Stepper Motor Driver Carrier
  MD09B3 = A4988 Stepper Motor Driver Carrier
  M1 = Stepper Motor - Bipolar  # not connected
  M2 = Stepper Motor - Bipolar  # not connected

nets:
  GND: Raspberry_Pi_1.GND, U1.GND
  N1: Raspberry_Pi_1.GIPO17, J1.pulse
  N2: Raspberry_Pi_1.GIPO27, J2.pulse
  N3: Raspberry_Pi_1.GIPO14, U1.DIN
  VCC: Raspberry_Pi_1.5V, U1.VCC, J2.vcc, J1.vcc, MD09B2.VDD, MD09B3.VDD
  GND_2: J2.gnd, J1.gnd, MD09B3.GROUND

custom parts:
  WS2812 RGB LED strip: WS2812 strip
